// Logisim project MiniMIPS.circ as structural Verilog
module PC (
  input  [31:0] in_1,
  output [31:0] out_2
);

  // Incrementer #(.width(30)) incrementer_1: pin names not known

  assign out_2[1:0] = in_1[1:0];
endmodule
